# Fritzing sketch putty (saved by Fritzing 0.9.3b)

parts:
  U1 = 1WBB [part_number=1 package=module]
  Part1 = FTDI Basic Programmer

nets:
  N1: U1.VBAT, Part1.POWER
  GND: U1.GND, Part1.GND
  N2: U1.UART_RX, Part1.TXO
  N3: U1.UART_TX, Part1.RXI

notes:
  3v mode

custom parts:
  1WBB: breakout for BLE radio RN4871
