# Fritzing sketch remote_light (saved by Fritzing 0.9.3b)
breadboards: 1

parts:
  U1 = 1WBB [part_number=1 package=module]
  R1 = Resistor [tolerance=±5% resistance=220 package=THT]
  LED1 = LED - 5mm [color="Red (633nm)" package="5 mm [THT]"]
  C1 = Ceramic Capacitor [capacitance=1mF package="100 mil [THT, multilayer]"]
  VCC1 = 4 x AAA Battery Mount

nets:
  N1: U1.VCC, LED1.anode, C1.0, VCC1.+
  N2: U1.GND#9, C1.1, VCC1.-
  N3: U1.P1_2, R1.Pin_1
  N4: R1.Pin_0, LED1.cathode

custom parts:
  1WBB: breakout for BLE radio RN4871
